# Fritzing sketch isp (saved by Fritzing 0.9.2b)
circuit board: 3.09034cm x 3.47133cm
breadboards: 1

parts:
  Arduino_UNO = Arduino Uno (Rev3)
  Heartbeat = LED - 5mm [color="Green (555nm)" package="5 mm [THT]"]
  ERROR = LED - 5mm [color="Red (633nm)" package="5 mm [THT]"]
  Programming = LED - 5mm [color="Blue (470nm)" package="5 mm [THT]"]
  Arduino_DUE = Arduino Due (Rev2b)  # not connected
  R2 = Resistor [tolerance=±5% resistance=220 package=THT]
  R1 = Resistor [tolerance=±5% resistance=220 package=THT]
  R3 = Resistor [tolerance=±5% resistance=220 package=THT]

nets:
  N1: Arduino_UNO.D8, ERROR.cathode, ERROR.anode, R2.Pin_1
  N2: Arduino_UNO.D9_PWM, Heartbeat.cathode, Heartbeat.anode, R3.Pin_1
  N3: Arduino_UNO.GND, R2.Pin_0, R1.Pin_0, R3.Pin_0
  N4: Arduino_UNO.D7, Programming.cathode, Programming.anode, R1.Pin_1
