# Fritzing sketch BluetoothDemo (saved by Fritzing 0.9.1b)
breadboards: 1

parts:
  Componente1 = Arduino Uno (Rev3)
  Componente2 = Bluetooth HC-05 Macho
  R1 = Resistor [tolerance=±5% resistance=1k package=THT]
  R2 = Resistor [tolerance=±5% resistance=2.2k package=THT]

nets:
  N1: Componente1.D0/RX, Componente2.TXD
  N2: Componente1.D1/TX, R1.Pin_0
  5V: Componente1.5V, Componente2.VCC
  GND: Componente1.GND, Componente2.GND, R2.Pin_1
  N3: Componente2.RXD, R1.Pin_1, R2.Pin_0
