# Fritzing sketch DHT22 (saved by Fritzing 0.9.0b)
circuit board: 6.40645cm x 5.03297cm
breadboards: 1

parts:
  Sensor_Reading = DHT22 Humidity and Temperature Sensor
  Arduino_Nano = Arduino Nano (Rev3.0)
  LED1 = LED - 3mm [color="Blue (470nm)" package="3 mm [THT]"]
  LED2 = LED - 3mm [color="Green (555nm)" package="3 mm [THT]"]
  LED3 = LED - 3mm [color="White (4500K)" package="3 mm [THT]"]
  LED4 = LED - 3mm [color="Yellow (585nm)" package="3 mm [THT]"]
  LED5 = LED - 3mm [color="Orange (605nm)" package="3 mm [THT]"]
  LED6 = LED - 3mm [color="Red (633nm)" package="3 mm [THT]"]
  R1 = Resistor [tolerance=±5% resistance=220 package=THT]

nets:
  VDD: Sensor_Reading.VDD, Arduino_Nano.5V
  N1: Sensor_Reading.DATA, Arduino_Nano.D2
  GND: Sensor_Reading.GND, Arduino_Nano.GND, R1.Pin_1
  N2: Arduino_Nano.D3, LED6.anode
  N3: Arduino_Nano.D4, LED5.anode
  N4: Arduino_Nano.D5, LED4.anode
  N5: Arduino_Nano.D6, LED3.anode
  N6: Arduino_Nano.D7, LED2.anode
  N7: Arduino_Nano.D8, LED1.anode
  N8: LED1.cathode, LED2.cathode, LED3.cathode, LED4.cathode, LED5.cathode, LED6.cathode, R1.Pin_0

notes:
  Using DHT22 breakout with 5.1k pullup resistor
