# Fritzing sketch NokiaLCD (saved by Fritzing 0.9.1b)
breadboards: 2

parts:
  Componente1 = Arduino Nano (Rev3.0)
  Nokia_5110_LCD_Module1 = Nokia5110LCDModule
  IC1 = '4050 Hex Buffer

nets:
  GND: Componente1.GND, Nokia_5110_LCD_Module1.Grnd, IC1.VSS
  VCC: Componente1.3V3, Nokia_5110_LCD_Module1.Vcc, Nokia_5110_LCD_Module1.LED, IC1.VCC

custom parts:
  : Nokia 5110 LCD with 8 pin. It's a 45mm*45mm module part. Description: The Nokia 5110 is a basic graphic LCD screen for lots of applications. It was originally intended for as a cell phone screen. This one is mounted on an easy to solder PCB. It uses the PCD8544 controller. The PCD8544 is a low power CMOS LCD controller/driver, designed to drive a graphic display of 48 rows and 84 columns. All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
